# Fritzing sketch iot_button_wemos (saved by Fritzing 0.9.3b)
circuit board: 5.23177cm x 2.93254cm

parts:
  U3 = LIPO-1000mAh [package=lipo-1000]
  WeMos_D1_Mini1 = WeMos D1 Mini
  S1 = Pushbutton [package="[SMD]"]

nets:
  N1: U3.+, WeMos_D1_Mini1.5V
  N2: U3.-, WeMos_D1_Mini1.G
  N3: WeMos_D1_Mini1.3V3, S1.Pin_4
  N4: WeMos_D1_Mini1.D8, S1.Pin_2
